# Fritzing sketch RFID Discrininator2 (saved by Fritzing 0.9.3b)

parts:
  Part1 = Arduino Uno (Rev3)
  M1 = Stepper Motor - Bipolar
  Part3 = EasyDriver_v44
  Power_plug1 = Power plug
  Part4 = Adafruit Datalogger Shield v1 [part_number="Adafruit #1141"]
  Board1 = RFID125KHzModuleforArduino  # not connected

nets:
  N1: Part1.A0, Part4.A0
  N2: Part1.A1, Part4.A1
  N3: Part1.A2, Part4.A2
  N4: Part1.A3, Part4.A3
  N5: Part1.A4/SDA, Part4.SDA
  N6: Part1.A5/SCL, Part4.SCL
  N7: Part1.D8, Part4.D8
  N8: Part1.D9_PWM, Part4.D9
  N9: Part1.D10_PWM/SS, Part4.SD_CS
  N10: Part1.D11_PWM/MOSI, Part4.MOSI
  N11: Part1.D12/MISO, Part4.MISO
  N12: Part1.D13/SCK, Part4.SCK
  GND: Part1.GND, Part3.GND, Power_plug1.GND, Part4.GND
  N13: Part1.AREF, Part4.AREF
  N14: Part1.D0/RX, Part4.D0
  N15: Part1.D1/TX, Part4.D1
  N16: Part1.D3_PWM, Part3.DIR, Part4.D3
  N17: Part1.D4, Part3.MS1, Part4.D4
  N18: Part1.D5_PWM, Part3.MS2, Part4.D5
  N19: Part1.D6_PWM, Part3.ENABLE, Part4.D6
  N20: Part1.D7, Part4.D7
  N21: Part1.ioref, Part4.IOREF
  N22: Part1.RESET, Part4.RESET
  3V3: Part1.3V3, Part4.3.3V
  VIN: Part1.VIN, Part4.VIN
  N23: Part1.N/C, Part4.NC
  N24: M1.A, Part3.OUT2A
  N25: M1.C, Part3.OUT2B
  N26: M1.B, Part3.OUT1A
  N27: M1.D, Part3.OUT1B
  N28: Part3.V+, Power_plug1.VCC
  VCC: Part3.VCC, Part4.+5V

notes:
  12V Motor power
  SeeedStudio 125kHz RFID
  Adafruit Data      Logger Shield
  EZdriver v4.5

custom parts:
  Adafruit Datalogger Shield v1: Here's a handy Arduino shield: we've had a lot of people looking for a dedicated and well-designed data logging shield. We worked hard to engineer an inexpensive but well-rounded design. Not only is it easy to assemble and customize, it also comes with great documentation and libraries. New! we now are carrying an 'assembled' version of this shield, with all the components pre-soldered. NOTE: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
  RFID125KHzModuleforArduino: RFID 125KHz Module for Arduino by Cooking Hacks
